// Logisim project adder8.circ as structural Verilog
module _8bitAdder (
  input  in_1,
  input  b0,
  input  c0,
  input  in_4,
  input  in_5,
  input  in_6,
  input  in_7,
  input  in_8,
  input  in_9,
  input  in_10,
  input  in_11,
  input  in_12,
  input  in_13,
  input  in_14,
  input  in_15,
  input  in_16,
  input  in_17,
  output out_18,
  output out_19,
  output out_20,
  output out_21,
  output out_22,
  output out_23,
  output out_24,
  output out_25
);

  wire adder_1_ci_1, adder_2_ci_1, adder_3_ci_1, adder_4_ci_1, adder_5_ci_1, adder_6_ci_1, adder_7_ci_1;

  adder adder_1 (.AI(in_1), .BI(b0), .CI(c0), .SUM(out_18), .CI_1(adder_1_ci_1));
  adder adder_2 (.AI(in_4), .BI(in_5), .CI(adder_1_ci_1), .SUM(out_19), .CI_1(adder_2_ci_1));
  adder adder_3 (.AI(in_6), .BI(in_7), .CI(adder_2_ci_1), .SUM(out_20), .CI_1(adder_3_ci_1));
  adder adder_4 (.AI(in_8), .BI(in_9), .CI(adder_3_ci_1), .SUM(out_21), .CI_1(adder_4_ci_1));
  adder adder_5 (.AI(in_10), .BI(in_11), .CI(adder_4_ci_1), .SUM(out_22), .CI_1(adder_5_ci_1));
  adder adder_6 (.AI(in_12), .BI(in_13), .CI(adder_5_ci_1), .SUM(out_23), .CI_1(adder_6_ci_1));
  adder adder_7 (.AI(in_14), .BI(in_15), .CI(adder_6_ci_1), .SUM(out_24), .CI_1(adder_7_ci_1));
  adder adder_8 (.AI(in_16), .BI(in_17), .CI(adder_7_ci_1), .SUM(out_25));  // open: CI_1

  // Notes on the sheet:
  //   a0
  //   a1
  //   b1
endmodule

module adder (
  input  AI,
  input  BI,
  input  CI,
  output SUM,
  output CI_1
);

  wire and_1_out, and_2_out, xor_1_out;

  xor xor_1 (xor_1_out, AI, BI);
  and and_1 (and_1_out, AI, BI);
  and and_2 (and_2_out, xor_1_out, CI);
  xor xor_2 (SUM, xor_1_out, CI);
  or or_1 (CI_1, and_1_out, and_2_out);
endmodule

module FA (
  input  in_1,
  input  [7:0] in_2,
  input  [7:0] in_3,
  output [7:0] out_4
);

  _8bitAdder u_8bitadder_1 (
    .out_18(out_4[0]), .out_19(out_4[1]), .out_20(out_4[2]), .out_21(out_4[3]), .out_22(out_4[4]),
    .out_23(out_4[5]), .out_24(out_4[6]), .out_25(out_4[7]), .in_1(in_1), .b0(in_2[0]), .c0(in_3[0]),
    .in_4(in_2[1]), .in_5(in_3[1]), .in_6(in_2[2]), .in_7(in_3[2]), .in_8(in_2[3]), .in_9(in_3[3]),
    .in_10(in_2[4]), .in_11(in_3[4]), .in_12(in_2[5]), .in_13(in_3[5]), .in_14(in_2[6]), .in_15(in_3[6]),
    .in_16(in_2[7]), .in_17(in_3[7]));
endmodule
